// Digital circuit mini_cpu.dig as structural Verilog
module mini_cpu (
  input  [7:0] M,
  input  [7:0] N,
  input  clk,
  input  [12:0] progIN,
  input  progLoad,
  input  result,
  input  reset,
  input  start,
  output [7:0] \output ,
  output valid,
  output done
);

  wire and_1_out, and_2_out, and_6_out, and_8_out, and_11_out, and_12_out, and_13_out, and_14_out,
       and_15_out, and_16_out, and_17_out, and_18_out, and_19_out, as, bs, comparator_1_eq, comparator_2_eq,
       comparator_4_eq, comparator_5_eq, comparator_7_eq, comparator_7_gt, comparator_7_lt, cs, d_ff_7_q,
       d_ff_9_q, d_ff_10_q, delay_1_out, eFlag, gFlag, jump, lcm, lFlag, multiplexer_23_out, or_2_out,
       or_3_out, or_4_out, or_5_out, or_6_out, or_7_out, or_8_out, or_10_out, or_11_out, or_12_out,
       or_14_out, or_15_out, prime_d, re, readRam, rehold, resetstop, restop, resulthold, sigB, sigComp,
       sigJump, sigJump_eq, sigJump_eq__gt, sigJump_gt, sigJump_lt, sigPrime, sigRam, slcm, st, starthold;
  wire [1:0] c_store_d, d_ff_14_q;
  wire [2:0] abc_store_d;
  wire [3:0] a_store_d, d_ff_11_q, sqrt_d;
  wire [4:0] d_ff_3_q, d_ff_5_q, delay_2_out, delay_3_out, multiplexer_3_out_2, multiplexer_4_out, opcode;
  wire [7:0] A, add_1_s, add_2_s, and_10_out, B, barrelshifter_1_out, C, counter_1_out, counter_2_out,
       d_ff_1_q, d_ff_6_q, delay_4_out, div_2_q, div_2_r, mul_2_mul, multiplexer_1_out, multiplexer_2_out,
       multiplexer_3_out, multiplexer_6_out, multiplexer_8_out, multiplexer_9_out, multiplexer_10_out,
       multiplexer_11_out, multiplexer_12_out, multiplexer_13_out, multiplexer_14_out, multiplexer_15_out,
       multiplexer_16_out, multiplexer_17_out, multiplexer_18_out, multiplexer_19_out, multiplexer_20_out,
       multiplexer_21_out, Noperand, not_1_out, operand, or_9_out, rA, ramdualaccess_1_d2, register_1_q,
       register_1_q_2, rom_2_d, sub_1_s, xor_1_out;
  wire [9:0] rom_3_d;
  wire [12:0] ramdualaccess_1_d1;
  wire [12:8] ramdualaccess_1_d2_2;
  wire [15:0] div_1_q, mul_1_mul, rom_1_d;
  wire [15:8] ramdualaccess_2_d2;

  and and_1 (and_1_out, or_2_out, ~re);  // And
  or or_1 (resulthold, result, and_2_out);
  and and_2 (and_2_out, ~restop, resulthold);  // And
  and and_3 (valid, or_2_out, ~st);  // And
  or or_2 (or_2_out, and_1_out, st);
  Multiplexer #(.Bits(8)) multiplexer_1 (.sel(or_3_out), .in_0({8{1'b0}}), .in_1(add_1_s), .out(multiplexer_1_out));
  or or_3 (or_3_out, progLoad, starthold);
  Multiplexer #(.Bits(8)) multiplexer_2 (.sel(jump), .in_0(multiplexer_1_out), .in_1(operand), .out(multiplexer_2_out));
  Add #(.Bits(8)) add_1 (.a(d_ff_1_q), .b(8'h1), .c_i(1'b0), .s(add_1_s));  // open: c_o
  D_FF #(.Bits(8)) d_ff_1 (.D(multiplexer_2_out), .C(clk), .Q(d_ff_1_q));  // open: nQ
  ROM #(.AddrBits(16), .Bits(16)) rom_1 (.A({ramdualaccess_2_d2, rA}), .sel(1'b1), .D(rom_1_d));
  and and_4 (done, ~re, ~result, ~st, or_4_out, ~progLoad);  // And
  or or_4 (or_4_out, restop, done);
  Mul #(.Bits(8)) mul_1 (.a(rA), .b(ramdualaccess_2_d2), .mul(mul_1_mul));
  D_FF d_ff_2 (.D(delay_1_out), .C(clk), .Q(re));  // open: nQ
  Delay delay_1 (.in(reset), .out(delay_1_out));
  Div #(.Bits(16)) div_1 (.a(mul_1_mul), .b(rom_1_d), .q(div_1_q));  // open: r
  and and_5 (rehold, ~resetstop, or_5_out);  // And
  or or_5 (or_5_out, re, and_6_out);
  and and_6 (and_6_out, ~resetstop, rehold);  // And
  Register #(.Bits(16)) register_1 (.D(div_1_q), .C(clk), .en(d_ff_7_q), .Q({register_1_q_2, register_1_q}));
  RAMDualAccess #(.AddrBits(8), .Bits(13)) ramdualaccess_1 (
    .str(progLoad), .C(clk), .ld(starthold), .A1(d_ff_1_q), .Din1(progIN), .A2(operand),
    .D1(ramdualaccess_1_d1), .D2({ramdualaccess_1_d2_2, ramdualaccess_1_d2}));
  D_FF #(.Bits(5)) d_ff_3 (.D(opcode), .C(clk), .Q(d_ff_3_q));  // open: nQ
  and and_7 (starthold, ~start, or_6_out);  // And
  or or_6 (or_6_out, start, and_8_out);
  D_FF d_ff_4 (.D(start), .C(clk), .Q(st));  // open: nQ
  Comparator #(.Bits(5)) comparator_1 (.a(opcode), .b({5{1'b1}}), .eq(comparator_1_eq));  // open: gt, lt
  Multiplexer #(.Bits(13)) multiplexer_3 (
    .sel(starthold), .in_0({13{1'b0}}), .in_1(ramdualaccess_1_d1),
    .out({multiplexer_3_out_2, multiplexer_3_out}));
  Counter #(.Bits(8)) counter_1 (.en(rehold), .C(clk), .clr(~rehold), .out(counter_1_out));  // open: ovf
  and and_8 (and_8_out, ~re, ~comparator_1_eq, or_6_out);  // And
  Multiplexer #(.Bits(5)) multiplexer_4 (.sel(jump), .in_0(delay_2_out), .in_1({5{1'b0}}), .out(multiplexer_4_out));
  Delay #(.Bits(5), .delayTime(2)) delay_2 (.in(multiplexer_3_out_2), .out(delay_2_out));
  Comparator #(.Bits(5)) comparator_2 (.a(d_ff_3_q), .b(5'b01001), .eq(comparator_2_eq));  // open: gt, lt
  D_FF #(.Bits(5)) d_ff_5 (.D(multiplexer_4_out), .C(clk), .Q(d_ff_5_q));  // open: nQ
  Multiplexer #(.Bits(8)) multiplexer_5 (
    .sel(comparator_2_eq), .in_0({8{1'b0}}), .in_1(ramdualaccess_1_d2), .out(Noperand));
  Comparator #(.Bits(8)) comparator_3 (.a(counter_1_out), .b(8'h10), .eq(resetstop));  // open: gt, lt
  Comparator #(.Bits(5)) comparator_4 (.a(5'b11110), .b(opcode), .eq(comparator_4_eq));  // open: gt, lt
  D_FF #(.Bits(8)) d_ff_6 (.D(multiplexer_3_out), .C(clk), .Q(d_ff_6_q));  // open: nQ
  Delay #(.Bits(5), .delayTime(2)) delay_3 (.in(d_ff_5_q), .out(delay_3_out));
  Multiplexer #(.Bits(8)) multiplexer_6 (.sel(rehold), .in_0(operand), .in_1(counter_1_out), .out(multiplexer_6_out));
  D_FF d_ff_7 (.D(comparator_4_eq), .C(clk), .Q(d_ff_7_q));  // open: nQ
  D_FF #(.Bits(8)) d_ff_8 (.D(d_ff_6_q), .C(clk), .Q(operand));  // open: nQ
  Multiplexer #(.Bits(5)) multiplexer_7 (.sel(jump), .in_0(delay_3_out), .in_1({5{1'b0}}), .out(opcode));
  Multiplexer #(.Bits(8)) multiplexer_8 (
    .sel(d_ff_7_q), .in_0(multiplexer_6_out), .in_1({4'b0000, operand[7:4]}), .out(multiplexer_8_out));
  Multiplexer #(.Bits(8)) multiplexer_9 (
    .sel(slcm), .in_0(register_1_q), .in_1(register_1_q_2), .out(multiplexer_9_out));
  D_FF d_ff_9 (.D(d_ff_7_q), .C(clk), .Q(d_ff_9_q));  // open: nQ
  Multiplexer #(.Bits(8)) multiplexer_10 (
    .sel(lcm), .in_0({8{1'b0}}), .in_1(multiplexer_9_out), .out(multiplexer_10_out));
  Multiplexer #(.Bits(8)) multiplexer_11 (
    .sel(d_ff_9_q), .in_0(multiplexer_8_out), .in_1(8'hf), .out(multiplexer_11_out));
  Multiplexer #(.Bits(8)) multiplexer_12 (
    .sel(or_7_out), .in_0(A), .in_1(multiplexer_10_out), .out(multiplexer_12_out));
  or or_7 (or_7_out, rehold, lcm);
  ROM #(.AddrBits(8), .Bits(4)) sqrt (.A(operand), .sel(1'b1), .D(sqrt_d));
  D_FF_AS d_ff_as_1 (.Set(1'b0), .D(d_ff_9_q), .C(d_ff_9_q), .Clr(d_ff_10_q), .Q(lcm));  // open: nQ
  Multiplexer #(.Bits(8)) multiplexer_13 (.sel(slcm), .in_0(multiplexer_11_out), .in_1(8'he), .out(multiplexer_13_out));
  Add #(.Bits(8)) add_2 (.a(A), .b(B), .c_i(1'b0), .s(add_2_s));  // open: c_o
  Sub #(.Bits(8)) sub_1 (.a(A), .b(B), .c_i(1'b0), .s(sub_1_s));  // open: c_o
  Mul #(.Bits(4)) mul_2 (.a(A[3:0]), .b(B[3:0]), .mul(mul_2_mul));
  Div #(.Bits(8)) div_2 (.a(A), .b(B), .q(div_2_q), .r(div_2_r));
  ROM #(.AddrBits(6), .Bits(8)) rom_2 (.A({A[2:0], B[2:0]}), .sel(as), .D(rom_2_d));
  and and_9 (slcm, lcm, ~d_ff_9_q);  // And
  or or_8 (or_8_out, rehold, lcm, sigRam);
  Counter #(.Bits(8)) counter_2 (.en(resulthold), .C(clk), .clr(restop), .out(counter_2_out));  // open: ovf
  Multiplexer #(.Bits(8)) multiplexer_14 (
    .sel(d_ff_7_q), .in_0(counter_2_out), .in_1({4'b0000, operand[3:0]}), .out(multiplexer_14_out));
  assign and_10_out = A & B;  // And and_10, 8 bits wide
  assign or_9_out = A | B;  // Or or_9, 8 bits wide
  assign xor_1_out = A ^ B;  // XOr xor_1, 8 bits wide
  BarrelShifter #(.Bits(8)) barrelshifter_1 (.in(A), .shift(B[3:0]), .out(barrelshifter_1_out));
  Comparator #(.Bits(8)) comparator_5 (.a(8'he), .b(multiplexer_13_out), .eq(comparator_5_eq));  // open: gt, lt
  RAMDualAccess #(.AddrBits(8), .Bits(8)) ramdualaccess_2 (
    .str(or_8_out), .C(clk), .ld(1'b1), .A1(multiplexer_13_out), .Din1(multiplexer_12_out),
    .A2(multiplexer_14_out), .D1(rA), .D2(ramdualaccess_2_d2));
  D_FF d_ff_10 (.D(comparator_5_eq), .C(clk), .Q(d_ff_10_q));  // open: nQ
  Comparator #(.Bits(8)) comparator_6 (.a(counter_2_out), .b(8'h11), .eq(restop));  // open: gt, lt
  assign not_1_out = ~A;  // Not not_1, 8 bits wide
  Multiplexer #(.Bits(8)) multiplexer_15 (
    .sel(resulthold), .in_0({8{1'b0}}), .in_1(ramdualaccess_2_d2), .out(multiplexer_15_out));
  Multiplexer #(.Selector_Bits(4), .Bits(8)) multiplexer_16 (
    .sel(d_ff_11_q), .in_0(operand), .in_1(B), .in_2(C), .in_3(Noperand), .in_4(rA), .in_5(add_2_s),
    .in_6(sub_1_s), .in_7(mul_2_mul), .in_8(div_2_q), .in_9(div_2_r), .in_10(rom_2_d), .in_11(not_1_out),
    .in_12(and_10_out), .in_13(or_9_out), .in_14(xor_1_out), .in_15(barrelshifter_1_out),
    .out(multiplexer_16_out));
  D_FF #(.Bits(4)) d_ff_11 (.D(a_store_d), .C(clk), .Q(d_ff_11_q));  // open: nQ
  Delay #(.Bits(8)) delay_4 (.in(multiplexer_15_out), .out(delay_4_out));
  Multiplexer #(.Bits(8)) multiplexer_17 (.sel(sigB), .in_0(A), .in_1(operand), .out(multiplexer_17_out));
  ROM #(.AddrBits(5), .Bits(4)) a_store (.A(opcode), .sel(1'b1), .D(a_store_d));
  D_FF #(.Bits(8)) d_ff_12 (.D(delay_4_out), .C(and_11_out), .Q(\output ));  // open: nQ
  and and_11 (and_11_out, clk, resulthold);
  Multiplexer #(.Bits(8)) multiplexer_18 (
    .sel(re), .in_0(multiplexer_16_out), .in_1({8{1'b0}}), .out(multiplexer_18_out));
  Register #(.Bits(8)) accA (.D(multiplexer_18_out), .C(clk), .en(or_10_out), .Q(A));
  or or_10 (or_10_out, as, re);
  Multiplexer #(.Bits(8)) multiplexer_19 (
    .sel(re), .in_0(multiplexer_17_out), .in_1({8{1'b0}}), .out(multiplexer_19_out));
  or or_11 (or_11_out, bs, re);
  Register #(.Bits(8)) accB (.D(multiplexer_19_out), .C(clk), .en(or_11_out), .Q(B));
  Seven_Seg_Hex seven_seg_hex_1 (.d(\output [7:4]), .dp(1'b0));
  ROM #(.AddrBits(5), .Bits(3)) abc_store (.A(opcode), .sel(1'b1), .D(abc_store_d));
  Seven_Seg_Hex seven_seg_hex_2 (.d(\output [3:0]), .dp(1'b0));
  D_FF #(.Bits(3)) d_ff_13 (.D(abc_store_d), .C(clk), .Q({as, bs, cs}));  // open: nQ
  ROM #(.AddrBits(5), .Bits(2)) c_store (.A(opcode), .sel(1'b1), .D(c_store_d));
  D_FF #(.Bits(2)) d_ff_14 (.D(c_store_d), .C(clk), .Q(d_ff_14_q));  // open: nQ
  Multiplexer #(.Selector_Bits(2), .Bits(8)) multiplexer_20 (
    .sel(d_ff_14_q), .in_0({8{1'b0}}), .in_1(A), .in_2(M), .in_3(N), .out(multiplexer_20_out));
  Comparator #(.Bits(8)) comparator_7 (.a(A), .b(B), .gt(comparator_7_gt), .eq(comparator_7_eq), .lt(comparator_7_lt));
  and and_12 (and_12_out, sigJump_eq, eFlag);
  Multiplexer #(.Bits(8)) multiplexer_21 (
    .sel(re), .in_0(multiplexer_20_out), .in_1({8{1'b0}}), .out(multiplexer_21_out));
  ROM #(.AddrBits(8)) prime (.A(A), .sel(1'b1), .D(prime_d));
  and and_13 (and_13_out, gFlag, ~re);  // And
  or or_12 (or_12_out, cs, re);
  Multiplexer multiplexer_22 (.sel(sigComp), .in_0(and_13_out), .in_1(comparator_7_gt), .out(gFlag));
  and and_14 (and_14_out, sigJump_gt, gFlag);
  Register #(.Bits(8)) regC (.D(multiplexer_21_out), .C(clk), .en(or_12_out), .Q(C));
  or or_13 (jump, and_12_out, and_14_out, and_15_out, and_16_out, and_19_out);
  and and_15 (and_15_out, sigJump, sigJump);
  Multiplexer multiplexer_23 (.sel(sigPrime), .in_0(comparator_7_eq), .in_1(prime_d), .out(multiplexer_23_out));
  and and_16 (and_16_out, sigJump_lt, lFlag);
  and and_17 (and_17_out, eFlag, ~re);  // And
  or or_14 (or_14_out, sigComp, sigPrime);
  and and_18 (and_18_out, lFlag, ~re);  // And
  ROM #(.AddrBits(5), .Bits(10)) rom_3 (.A(opcode), .sel(1'b1), .D(rom_3_d));
  and and_19 (and_19_out, sigJump_eq__gt, or_15_out);
  Multiplexer multiplexer_24 (.sel(or_14_out), .in_0(and_17_out), .in_1(multiplexer_23_out), .out(eFlag));
  Multiplexer multiplexer_25 (.sel(sigComp), .in_0(and_18_out), .in_1(comparator_7_lt), .out(lFlag));
  D_FF #(.Bits(10)) d_ff_15 (
    .D(rom_3_d), .C(clk),
    .Q({readRam, sigPrime, sigComp, sigJump_eq__gt, sigJump_lt, sigJump_gt, sigJump_eq, sigJump, sigRam, sigB}));  // open: nQ
  or or_15 (or_15_out, eFlag, gFlag);

  // Other names for the same wires on the sheet: in[12:0] = progIN; load = progLoad; retemp = result

  // Notes on the sheet:
  //   result hold
  //   valid
  //   pRAM
  //   rRAM
  //   Done
  //   reset hold
  //   contents of rom_1 (hex, n*v repeats v):
  //   0,1,2,3,4,5,6,7,8,9,a,b,c,d,e,f,10,11,12,13,14,15,16,17,18,19
  //   ,1a,1b,1c,1d,1e,1f,20,21,22,23,24,25,26,27,28,29,2a,2b,2c,2d,2e
  //   ,2f,30,31,32,33,34,35,36,37,38,39,3a,3b,3c,3d,3e,3f,40,41,42,43
  //   ,44,45,46,47,48,49,4a,4b,4c,4d,4e,4f,50,51,52,53,54,55,56,57,58
  //   ,59,5a,5b,5c,5d,5e,5f,60,61,62,63,64,65,66,67,68,69,6a,6b,6c,6d
  //   ,6e,6f,70,71,72,73,74,75,76,77,78,79,7a,7b,7c,7d,7e,7f,80,81,82
  //   ,83,84,85,86,87,88,89,8a,8b,8c,8d,8e,8f,90,91,92,93,94,95,96,97
  //   ,98,99,9a,9b,9c,9d,9e,9f,a0,a1,a2,a3,a4,a5,a6,a7,a8,a9,aa,ab,ac
  //   ,ad,ae,af,b0,b1,b2,b3,b4,b5,b6,b7,b8,b9,ba,bb,bc,bd,be,bf,c0,c1
  //   ,c2,c3,c4,c5,c6,c7,c8,c9,ca,cb,cc,cd,ce,cf,d0,d1,d2,d3,d4,d5,d6
  //   ,d7,d8,d9,da,db,dc,dd,de,df,e0,e1,e2,e3,e4,e5,e6,e7,e8,e9,ea,eb
  //   ,ec,ed,ee,ef,f0,f1,f2,f3,f4,f5,f6,f7,f8,f9,fa,fb,fc,fd,fe,ff,256*1
  //   ,2,1,2,1,2,1,2,1,2,1,2,1,2,1,2,1,2,1,2,1,2,1,2,1,2,1,2,1,2,1,2
  //   ,1,2,1,2,1,2,1,2,1,2,1,2,1,2,1,2,1,2,1,2,1,2,1,2,1,2,1,2,1,2,1
  //   ,2,1,2,1,2,1,2,1,2,1,2,1,2,1,2,1,2,1,2,1,2,1,2,1,2,1,2,1,2,1,2
  //   ,1,2,1,2,1,2,1,2,1,2,1,2,1,2,1,2,1,2,1,2,1,2,1,2,1,2,1,2,1,2,1
  //   ,2,1,2,1,2,1,2,1,2,1,2,1,2,1,2,1,2,1,2,1,2,1,2,1,2,1,2,1,2,1,2
  //   ,1,2,1,2,1,2,1,2,1,2,1,2,1,2,1,2,1,2,1,2,1,2,1,2,1,2,1,2,1,2,1
  //   ,2,1,2,1,2,1,2,1,2,1,2,1,2,1,2,1,2,1,2,1,2,1,2,1,2,1,2,1,2,1,2
  //   ,1,2,1,2,1,2,1,2,1,2,1,2,1,2,1,2,1,2,1,2,1,2,1,2,1,2,1,2,1,2,1
  //   ,2,1,2,1,2,1,2,1,3,1,1,3,1,1,3,1,1,3,1,1,3,1,1,3,1,1,3,1,1,3,1,1
  //   ,3,1,1,3,1,1,3,1,1,3,1,1,3,1,1,3,1,1,3,1,1,3,1,1,3,1,1,3,1,1,3
  //   ,1,1,3,1,1,3,1,1,3,1,1,3,1,1,3,1,1,3,1,1,3,1,1,3,1,1,3,1,1,3,1,1
  //   ,3,1,1,3,1,1,3,1,1,3,1,1,3,1,1,3,1,1,3,1,1,3,1,1,3,1,1,3,1,1,3
  //   ,1,1,3,1,1,3,1,1,3,1,1,3,1,1,3,1,1,3,1,1,3,1,1,3,1,1,3,1,1,3,1,1
  //   ,3,1,1,3,1,1,3,1,1,3,1,1,3,1,1,3,1,1,3,1,1,3,1,1,3,1,1,3,1,1,3
  //   ,1,1,3,1,1,3,1,1,3,1,1,3,1,1,3,1,1,3,1,1,3,1,1,3,1,1,3,1,1,3,1,1
  //   ,3,1,1,3,1,1,3,1,1,3,1,1,3,1,1,3,1,1,3,1,1,3,1,1,3,1,1,3,1,1,3
  //   ,1,1,3,1,1,3,1,1,3,1,1,3,4,1,2,1,4,1,2,1,4,1,2,1,4,1,2,1,4,1,2
  //   ,1,4,1,2,1,4,1,2,1,4,1,2,1,4,1,2,1,4,1,2,1,4,1,2,1,4,1,2,1,4,1
  //   ,2,1,4,1,2,1,4,1,2,1,4,1,2,1,4,1,2,1,4,1,2,1,4,1,2,1,4,1,2,1,4
  //   ,1,2,1,4,1,2,1,4,1,2,1,4,1,2,1,4,1,2,1,4,1,2,1,4,1,2,1,4,1,2,1
  //   ,4,1,2,1,4,1,2,1,4,1,2,1,4,1,2,1,4,1,2,1,4,1,2,1,4,1,2,1,4,1,2
  //   ,1,4,1,2,1,4,1,2,1,4,1,2,1,4,1,2,1,4,1,2,1,4,1,2,1,4,1,2,1,4,1
  //   ,2,1,4,1,2,1,4,1,2,1,4,1,2,1,4,1,2,1,4,1,2,1,4,1,2,1,4,1,2,1,4
  //   ,1,2,1,4,1,2,1,4,1,2,1,4,1,2,1,4,1,2,1,4,1,2,1,4,1,2,1,4,1,2,1
  //   ,4,1,2,1,4,1,2,1,4,1,2,1,4,1,2,1,4,1,2,1,5,4*1,5,4*1,5,4*1,5,4*1
  //   ,5,4*1,5,4*1,5,4*1,5,4*1,5,4*1,5,4*1,5,4*1,5,4*1,5,4*1,5,4*1,5
  //   ,4*1,5,4*1,5,4*1,5,4*1,5,4*1,5,4*1,5,4*1,5,4*1,5,4*1,5,4*1,5,4*1
  //   ,5,4*1,5,4*1,5,4*1,5,4*1,5,4*1,5,4*1,5,4*1,5,4*1,5,4*1,5,4*1,5
  //   ,4*1,5,4*1,5,4*1,5,4*1,5,4*1,5,4*1,5,4*1,5,4*1,5,4*1,5,4*1,5,4*1
  //   ,5,4*1,5,4*1,5,4*1,5,4*1,5,4*1,5,6,1,2,3,2,1,6,1,2,3,2,1,6,1,2
  //   ,3,2,1,6,1,2,3,2,1,6,1,2,3,2,1,6,1,2,3,2,1,6,1,2,3,2,1,6,1,2,3
  //   ,2,1,6,1,2,3,2,1,6,1,2,3,2,1,6,1,2,3,2,1,6,1,2,3,2,1,6,1,2,3,2
  //   ,1,6,1,2,3,2,1,6,1,2,3,2,1,6,1,2,3,2,1,6,1,2,3,2,1,6,1,2,3,2,1
  //   ,6,1,2,3,2,1,6,1,2,3,2,1,6,1,2,3,2,1,6,1,2,3,2,1,6,1,2,3,2,1,6
  //   ,1,2,3,2,1,6,1,2,3,2,1,6,1,2,3,2,1,6,1,2,3,2,1,6,1,2,3,2,1,6,1
  //   ,2,3,2,1,6,1,2,3,2,1,6,1,2,3,2,1,6,1,2,3,2,1,6,1,2,3,2,1,6,1,2
  //   ,3,2,1,6,1,2,3,2,1,6,1,2,3,2,1,6,1,2,3,2,1,6,1,2,3,2,1,6,1,2,3
  //   ,2,1,6,1,2,3,2,1,6,1,2,3,2,1,6,1,2,3,2,1,6,1,2,3,7,6*1,7,6*1,7
  //   ,6*1,7,6*1,7,6*1,7,6*1,7,6*1,7,6*1,7,6*1,7,6*1,7,6*1,7,6*1,7,6*1
  //   ,7,6*1,7,6*1,7,6*1,7,6*1,7,6*1,7,6*1,7,6*1,7,6*1,7,6*1,7,6*1,7
  //   ,6*1,7,6*1,7,6*1,7,6*1,7,6*1,7,6*1,7,6*1,7,6*1,7,6*1,7,6*1,7,6*1
  //   ,7,6*1,7,6*1,7,1,1,1,8,1,2,1,4,1,2,1,8,1,2,1,4,1,2,1,8,1,2,1,4
  //   ,1,2,1,8,1,2,1,4,1,2,1,8,1,2,1,4,1,2,1,8,1,2,1,4,1,2,1,8,1,2,1
  //   ,4,1,2,1,8,1,2,1,4,1,2,1,8,1,2,1,4,1,2,1,8,1,2,1,4,1,2,1,8,1,2
  //   ,1,4,1,2,1,8,1,2,1,4,1,2,1,8,1,2,1,4,1,2,1,8,1,2,1,4,1,2,1,8,1
  //   ,2,1,4,1,2,1,8,1,2,1,4,1,2,1,8,1,2,1,4,1,2,1,8,1,2,1,4,1,2,1,8
  //   ,1,2,1,4,1,2,1,8,1,2,1,4,1,2,1,8,1,2,1,4,1,2,1,8,1,2,1,4,1,2,1
  //   ,8,1,2,1,4,1,2,1,8,1,2,1,4,1,2,1,8,1,2,1,4,1,2,1,8,1,2,1,4,1,2
  //   ,1,8,1,2,1,4,1,2,1,8,1,2,1,4,1,2,1,8,1,2,1,4,1,2,1,8,1,2,1,4,1
  //   ,2,1,8,1,2,1,4,1,2,1,8,1,2,1,4,1,2,1,9,1,1,3,1,1,3,1,1,9,1,1,3
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  //   start hold
  //   opcode(store ABC)
  //   contents of sqrt (hex, n*v repeats v):
  //   0,1,1,1,5*2,7*3,9*4,11*5,12*6,16*7,16*8,20*9,21*a,23*b,25*c,27*d
  //   ,29*e,31*f
  //   contents of rom_2 (hex, n*v repeats v):
  //   1,7*0,9*1,2,4,8,10,20,40,80,1,3,9,1b,51,f3,d9,8b,1,4,10,40,a00
  //   ,0,0,0,1,5,19,7d,71,35,9,2d,1,6,24,d8,10,60,40,80,1,7,31,57,61
  //   ,a7,91,f7
  //   contents of a_store (hex, n*v repeats v):
  //   0,0,0,1,0,0,2,0,0,3,4,6*0,5,6,7,8,9,a,0,b,c,d,e,f
  //   contents of abc_store (hex, n*v repeats v):
  //   0,4,2,4,2,1,4,1,1,4,4,6*0,6*4,0,5*4
  //   contents of c_store (hex, n*v repeats v):
  //   5*0,1,0,2,3
  //   opcode(comp&prime)
  //   opcode(Jump)
  //   contents of prime (hex, n*v repeats v):
  //   0,0,1,1,0,1,0,1,0,0,0,1,0,1,0,0,0,1,0,1,0,0,0,1,5*0,1,0,1,5*0
  //   ,1,0,0,0,1,0,1,0,0,0,1,5*0,1,5*0,1,0,1,5*0,1,0,0,0,1,0,1,5*0,1
  //   ,0,0,0,1,5*0,1,7*0,1,0,0,0,1,0,1,0,0,0,1,0,1,0,0,0,1,13*0,1,0,0,0
  //   ,1,5*0,1,0,1,9*0,1,0,1,5*0,1,5*0,1,0,0,0,1,5*0,1,5*0,1,0,1,9*0
  //   ,1,0,1,0,0,0,1,0,1,11*0,1,11*0,1,0,0,0,1,0,1,0,0,0,1,5*0,1,0,1
  //   ,9*0,1
  //   contents of rom_3 (hex, n*v repeats v):
  //   0,0,1,7*0,200,2,4,8,10,20,40,6*0,80,5*0,100
endmodule
